// Digital circuit Control.dig as structural Verilog
// Control unit module.
module Control (
  input  nCLOCK,
  input  [7:0] IR_IN,
  output HALT,
  output PC_COUNT,
  output ALU_SUBTRACT,
  output OUT_SIGNED,
  output CONST_BUS_nOUT,
  output RAM_BUS_nOUT,
  output PC_BUS_nOUT,
  output IR_BUS_nOUT,
  output REGA_BUS_nOUT,
  output REGB_BUS_nOUT,
  output ALU_BUS_nOUT,
  output RAM_BUS_nIN,
  output MAR_BUS_nIN,
  output PC_BUS_nIN,
  output IR_BUS_nIN,
  output REGA_BUS_nIN,
  output REGB_BUS_nIN,
  output OUT_BUS_nIN
);

  wire _74161_1_pin9, BUS_OUT_0, BUS_OUT_6;
  wire [2:0] BUS_IN_ADDRESS, BUS_OUT_ADDRESS;
  wire [3:0] ADDRESS;
  wire [7:2] CONTROL_HIGH;

  // Probe on ADDRESS
  _74161 _74161_1 (
    .pin1(1'b1), .pin2(nCLOCK), .pin3(1'b0), .pin4(1'b0), .pin5(1'b0), .pin6(1'b0), .pin7(1'b1), .pin8(1'b0),
    .pin9(_74161_1_pin9), .pin10(1'b1), .pin11(ADDRESS[3]), .pin12(ADDRESS[2]), .pin13(ADDRESS[1]),
    .pin14(ADDRESS[0]), .pin16(1'b1));  // open: pin15
  EEPROM #(.AddrBits(11), .Bits(8)) eeprom_1 (
    .A({3'b000, IR_IN[7:4], ADDRESS}), .CS(~1'b0), .WE(~1'b1), .OE(~1'b0),
    .D({CONTROL_HIGH, OUT_SIGNED, ALU_SUBTRACT}));
  LED led_1 (.in(IR_IN[0]));
  LED led_2 (.in(IR_IN[1]));
  LED led_3 (.in(IR_IN[2]));
  LED led_4 (.in(IR_IN[3]));
  // Probe on {3'b000, IR_IN[7:4], ADDRESS}
  // Probe on {CONTROL_HIGH, OUT_SIGNED, ALU_SUBTRACT}
  // Probe on IR_IN[7:4]
  not not_1 (_74161_1_pin9, CONTROL_HIGH[7]);
  EEPROM #(.AddrBits(11), .Bits(8)) eeprom_2 (
    .A({3'b000, IR_IN[7:4], ADDRESS}), .CS(~1'b0), .WE(~1'b1), .OE(~1'b0),
    .D({PC_COUNT, HALT, BUS_IN_ADDRESS, BUS_OUT_ADDRESS}));
  _74138 u_BUS_OUT_ADDRESS (
    .pin1(BUS_OUT_ADDRESS[0]), .pin2(BUS_OUT_ADDRESS[1]), .pin3(BUS_OUT_ADDRESS[2]), .pin4(1'b0),
    .pin5(1'b0), .pin6(1'b1), .pin7(BUS_OUT_6), .pin8(1'b0), .pin9(ALU_BUS_nOUT), .pin10(REGB_BUS_nOUT),
    .pin11(REGA_BUS_nOUT), .pin12(IR_BUS_nOUT), .pin13(PC_BUS_nOUT), .pin14(RAM_BUS_nOUT), .pin15(BUS_OUT_0),
    .pin16(1'b1));
  // Probe on {PC_COUNT, HALT, BUS_IN_ADDRESS, BUS_OUT_ADDRESS}
  // Probe on BUS_OUT_ADDRESS
  and and_1 (CONST_BUS_nOUT, BUS_OUT_0, BUS_OUT_6);
  _74138 u_BUS_IN_ADDRESS (
    .pin1(BUS_IN_ADDRESS[0]), .pin2(BUS_IN_ADDRESS[1]), .pin3(BUS_IN_ADDRESS[2]), .pin4(1'b0), .pin5(1'b0),
    .pin6(1'b1), .pin7(OUT_BUS_nIN), .pin8(1'b0), .pin9(REGB_BUS_nIN), .pin10(REGA_BUS_nIN),
    .pin11(IR_BUS_nIN), .pin12(PC_BUS_nIN), .pin13(MAR_BUS_nIN), .pin14(RAM_BUS_nIN), .pin16(1'b1));  // open: pin15
  // Probe on BUS_IN_ADDRESS

  // Other names for the same wires on the sheet: STEP[3:0] = ADDRESS; CONTROL_HIGH[1:0] = {OUT_SIGNED, ALU_SUBTRACT};
  //   INSTRUCTION_COMPLETE = CONTROL_HIGH[7]; CONTROL_LOW[7:0] = {PC_COUNT, HALT, BUS_IN_ADDRESS, BUS_OUT_ADDRESS};
  //   ADDRESS[7:4] = IR_IN[7:4]; IR_HIGH[3:0] = IR_IN[7:4]

  // Notes on the sheet:
  //   contents of eeprom_1 (hex, n*v repeats v):
  //   0,80,0,0,0,0,0,0,0,0,0,0,0,0,0,0,0,0,0,80
  //   contents of eeprom_2 (hex, n*v repeats v):
  //   12,a1,40,40,40,40,40,40,40,40,40,40,40,40,40,40,12,a1,13,29,40,40,40,40,40,40,40,
  //   40,40,40,40,40,40,40,40,40,40,40,40,40,40,40,40,40,40,40,40,40,40,40,40,40,40,40,
  //   40,40,40,40,40,40,40,40,40,40,40,40,40,40,40,40,40,40,40,40,40,40,40,40,40,40,40,
  //   40,40,40,40,40,40,40,40,40,40,40,40,40,40,40,40,40,40,40,40,40,40,40,40,40,40,40,
  //   40,40,40,40,40,40,40,40,40,40,40,40,40,40,40,40,40,40,40,40,40,40,40,40,40,40,40,
  //   40,40,40,40,40,40,40,40,40,40,40,40,40,40,40,40,40,40,40,40,40,40,40,40,40,40,40,
  //   40,40,40,40,40,40,40,40,40,40,40,40,40,40,40,40,40,40,40,40,40,40,40,40,40,40,40,
  //   40,40,40,40,40,40,40,40,40,40,40,40,40,40,40,40,40,40,40,40,40,40,40,40,40,40,40,
  //   40,40,40,40,40,40,40,40,40,40,40,40,40,40,40,40,40,40,40,40,40,40,40,40,40,40,40,
  //   40,40,40,40,40,40,40,40,40,40,40,40,40
endmodule
