// Digital circuit Mar.dig as structural Verilog
// Memory address register module.
module Mar (
  input  CLOCK,
  input  [7:0] BUS,
  input  BUS_nIN,
  output [7:0] OUT
);

  _74377 _74377_1 (
    .pin1(BUS_nIN), .pin2(OUT[0]), .pin3(BUS[0]), .pin4(BUS[1]), .pin5(OUT[1]), .pin6(OUT[2]), .pin7(BUS[2]),
    .pin8(BUS[3]), .pin9(OUT[3]), .pin10(1'b0), .pin11(CLOCK), .pin12(OUT[4]), .pin13(BUS[4]),
    .pin14(BUS[5]), .pin15(OUT[5]), .pin16(OUT[6]), .pin17(BUS[6]), .pin18(BUS[7]), .pin19(OUT[7]),
    .pin20(1'b1));

  // Other names for the same wires on the sheet: D0 = BUS[0]; D1 = BUS[1]; D2 = BUS[2]; D3 = BUS[3]; D4 = BUS[4];
  //   D5 = BUS[5]; D6 = BUS[6]; D7 = BUS[7]; Q0 = OUT[0]; Q1 = OUT[1]; Q2 = OUT[2]; Q3 = OUT[3]; Q4 = OUT[4];
  //   Q5 = OUT[5]; Q6 = OUT[6]; Q7 = OUT[7]

  // Notes on the sheet:
  //   BUS_nIN: default 1
endmodule
