// Digital circuit Processor.dig as structural Verilog
module Processor (
  input  CLOCK
);

  wire _1s, _10s, _100s, a, ALU_BUS_nOUT, ALU_BUS_OUT, ALU_SUBTRACT, b, c, CONST_BUS_nOUT, d, e, f, g, HALT,
       IR_BUS_IN, IR_BUS_nIN, IR_BUS_nOUT, IR_BUS_OUT, MAR_BUS_IN, MAR_BUS_nIN, nCLOCK, OUT_BUS_IN,
       OUT_BUS_nIN, OUT_SIGNED, PC_BUS_IN, PC_BUS_nIN, PC_BUS_nOUT, PC_BUS_OUT, PC_COUNT, RAM_BUS_IN,
       RAM_BUS_nIN, RAM_BUS_nOUT, RAM_BUS_OUT, REGA_BUS_IN, REGA_BUS_nIN, REGA_BUS_nOUT, REGA_BUS_OUT,
       REGB_BUS_IN, REGB_BUS_nIN, REGB_BUS_nOUT, REGB_BUS_OUT, SIGN;
  wire [7:0] BUS, OUT_IR, OUT_MAR, OUT_REG_B, PEEK_ALU, PEEK_PC, PEEK_RAM, REG_A;

  Stop u_HALT (.stop(HALT));
  Pc pc_1 (.CLOCK(CLOCK), .COUNT(PC_COUNT), .nIN_BUS(PC_BUS_nIN), .nOUT_BUS(PC_BUS_nOUT), .BUS(BUS), .PEEK(PEEK_PC));
  Ram ram_1 (
    .CLOCK(CLOCK), .ADDRESS(OUT_MAR), .nIN_BUS(RAM_BUS_nIN), .nOUT_BUS(RAM_BUS_nOUT), .BUS(BUS),
    .PEEK(PEEK_RAM));
  Mar mar_1 (.CLOCK(CLOCK), .BUS(BUS), .BUS_nIN(MAR_BUS_nIN), .OUT(OUT_MAR));
  Ir ir_1 (.CLOCK(CLOCK), .BUS_nIN(IR_BUS_nIN), .BUS_nOUT(IR_BUS_nOUT), .BUS(BUS), .OUT(OUT_IR));
  Register u_A (.CLOCK(CLOCK), .nIN_BUS(REGA_BUS_nIN), .nOUT_BUS(REGA_BUS_nOUT), .BUS(BUS), .OUTPUT(REG_A));
  Register u_B (.CLOCK(CLOCK), .nIN_BUS(REGB_BUS_nIN), .nOUT_BUS(REGB_BUS_nOUT), .BUS(BUS), .OUTPUT(OUT_REG_B));
  Alu alu_1 (
    .A(REG_A), .B(OUT_REG_B), .SUBTRACT(ALU_SUBTRACT), .BUS_nOUT(ALU_BUS_nOUT), .BUS(BUS), .OUT(PEEK_ALU));  // open: CARRY
  Out out_1 (
    .CLOCK(CLOCK), .REFRESH(CLOCK), .BUS(BUS), .SIGNED(OUT_SIGNED), .nIN_BUS(OUT_BUS_nIN),
    .PLACE({SIGN, _100s, _10s, _1s}), .OUTPUT_7SEG({a, b, c, d, e, f, g}));
  // Control control_1: pin names not known; wires that end beside it: nCLOCK, OUT_IR, HALT, PC_COUNT, ALU_SUBTRACT, OUT_SIGNED, CONST_BUS_nOUT, RAM_BUS_nOUT, PC_BUS_nOUT, IR_BUS_nOUT, REGA_BUS_nOUT, REGB_BUS_nOUT, ALU_BUS_nOUT, RAM_BUS_nIN, MAR_BUS_nIN, PC_BUS_nIN, IR_BUS_nIN, REGA_BUS_nIN, REGB_BUS_nIN, OUT_BUS_nIN
  not not_1 (nCLOCK, CLOCK);
  // Probe ~CLOCK on nCLOCK
  LED led_1 (.in(BUS[7]));
  LED led_2 (.in(PEEK_PC[7]));
  LED led_3 (.in(PEEK_RAM[7]));
  LED led_4 (.in(OUT_MAR[7]));
  LED led_5 (.in(OUT_IR[7]));
  LED led_6 (.in(REG_A[7]));
  LED led_7 (.in(OUT_REG_B[7]));
  LED led_8 (.in(PEEK_ALU[7]));
  LED led_9 (.in(BUS[3]));
  LED led_10 (.in(BUS[4]));
  LED led_11 (.in(BUS[5]));
  LED led_12 (.in(BUS[6]));
  LED led_13 (.in(PEEK_PC[3]));
  LED led_14 (.in(PEEK_PC[4]));
  LED led_15 (.in(PEEK_PC[5]));
  LED led_16 (.in(PEEK_PC[6]));
  LED led_17 (.in(PEEK_RAM[3]));
  LED led_18 (.in(PEEK_RAM[4]));
  LED led_19 (.in(PEEK_RAM[5]));
  LED led_20 (.in(PEEK_RAM[6]));
  LED led_21 (.in(OUT_MAR[3]));
  LED led_22 (.in(OUT_MAR[4]));
  LED led_23 (.in(OUT_MAR[5]));
  LED led_24 (.in(OUT_MAR[6]));
  LED led_25 (.in(OUT_IR[3]));
  LED led_26 (.in(OUT_IR[4]));
  LED led_27 (.in(OUT_IR[5]));
  LED led_28 (.in(OUT_IR[6]));
  LED led_29 (.in(REG_A[3]));
  LED led_30 (.in(REG_A[4]));
  LED led_31 (.in(REG_A[5]));
  LED led_32 (.in(REG_A[6]));
  LED led_33 (.in(OUT_REG_B[3]));
  LED led_34 (.in(OUT_REG_B[4]));
  LED led_35 (.in(OUT_REG_B[5]));
  LED led_36 (.in(OUT_REG_B[6]));
  LED led_37 (.in(PEEK_ALU[3]));
  LED led_38 (.in(PEEK_ALU[4]));
  LED led_39 (.in(PEEK_ALU[5]));
  LED led_40 (.in(PEEK_ALU[6]));
  LED led_41 (.in(HALT));
  LED led_42 (.in(PC_COUNT));
  LED led_43 (.in(ALU_SUBTRACT));
  LED led_44 (.in(OUT_SIGNED));
  LED led_45 (.in(BUS[0]));
  LED led_46 (.in(BUS[1]));
  LED led_47 (.in(BUS[2]));
  LED led_48 (.in(PEEK_PC[0]));
  LED led_49 (.in(PEEK_PC[1]));
  LED led_50 (.in(PEEK_PC[2]));
  LED led_51 (.in(PEEK_RAM[0]));
  LED led_52 (.in(PEEK_RAM[1]));
  LED led_53 (.in(PEEK_RAM[2]));
  LED led_54 (.in(OUT_MAR[0]));
  LED led_55 (.in(OUT_MAR[1]));
  LED led_56 (.in(OUT_MAR[2]));
  LED led_57 (.in(OUT_IR[0]));
  LED led_58 (.in(OUT_IR[1]));
  LED led_59 (.in(OUT_IR[2]));
  LED led_60 (.in(REG_A[0]));
  LED led_61 (.in(REG_A[1]));
  LED led_62 (.in(REG_A[2]));
  LED led_63 (.in(OUT_REG_B[0]));
  LED led_64 (.in(OUT_REG_B[1]));
  LED led_65 (.in(OUT_REG_B[2]));
  LED led_66 (.in(PEEK_ALU[0]));
  LED led_67 (.in(PEEK_ALU[1]));
  LED led_68 (.in(PEEK_ALU[2]));
  LED led_69 (.in(RAM_BUS_OUT));
  LED led_70 (.in(PC_BUS_OUT));
  LED led_71 (.in(REGA_BUS_OUT));
  LED led_72 (.in(IR_BUS_OUT));
  LED led_73 (.in(REGB_BUS_OUT));
  LED led_74 (.in(ALU_BUS_OUT));
  LED led_75 (.in(RAM_BUS_IN));
  LED led_76 (.in(MAR_BUS_IN));
  LED led_77 (.in(PC_BUS_IN));
  LED led_78 (.in(REGA_BUS_IN));
  LED led_79 (.in(REGB_BUS_IN));
  LED led_80 (.in(IR_BUS_IN));
  Seven_Seg #(.commonCathode("true"), .ledPersistence("true")) seven_seg_1 (
    .a(a), .b(b), .c(c), .d(d), .e(e), .f(f), .g(g), .dp(1'b0), .common(SIGN));
  LED led_81 (.in(OUT_BUS_IN));
  Seven_Seg #(.commonCathode("true"), .ledPersistence("true")) seven_seg_2 (
    .a(a), .b(b), .c(c), .d(d), .e(e), .f(f), .g(g), .dp(1'b0), .common(_100s));
  not not_2 (RAM_BUS_OUT, RAM_BUS_nOUT);
  not not_3 (PC_BUS_OUT, PC_BUS_nOUT);
  not not_4 (IR_BUS_OUT, IR_BUS_nOUT);
  not not_5 (REGA_BUS_OUT, REGA_BUS_nOUT);
  not not_6 (REGB_BUS_OUT, REGB_BUS_nOUT);
  not not_7 (ALU_BUS_OUT, ALU_BUS_nOUT);
  not not_8 (RAM_BUS_IN, RAM_BUS_nIN);
  not not_9 (MAR_BUS_IN, MAR_BUS_nIN);
  not not_10 (PC_BUS_IN, PC_BUS_nIN);
  not not_11 (IR_BUS_IN, IR_BUS_nIN);
  not not_12 (REGA_BUS_IN, REGA_BUS_nIN);
  not not_13 (REGB_BUS_IN, REGB_BUS_nIN);
  not not_14 (OUT_BUS_IN, OUT_BUS_nIN);
  Seven_Seg #(.commonCathode("true"), .ledPersistence("true")) seven_seg_3 (
    .a(a), .b(b), .c(c), .d(d), .e(e), .f(f), .g(g), .dp(1'b0), .common(_10s));
  assign BUS = ~CONST_BUS_nOUT ? {8{1'b1}} : 8'bz;  // DriverInvSel driverinvsel_1
  Seven_Seg #(.commonCathode("true"), .ledPersistence("true")) seven_seg_4 (
    .a(a), .b(b), .c(c), .d(d), .e(e), .f(f), .g(g), .dp(1'b0), .common(_1s));

  // Notes on the sheet:
  //   CLOCK: Hz: 2
  //   Digital workaround as leds can only be connected from cathode
endmodule
